# Fritzing sketch tinlight (saved by Fritzing 0.9.3b)
breadboards: 1

parts:
  Part1 = Arduino Pro Mini v13
  S1 = Taiway 100-SP-X-T1 SPDT Miniature Toggle Switch [part_number=100-SP-X-T1-0-0-B1-M2 package=THT]
  S2 = Taiway 100-SP-X-T1 SPDT Miniature Toggle Switch [part_number=100-SP-X-T1-0-0-B1-M2 package=THT]
  NEOPIXEL1 = Neopixel Strip -- White (30/m)

nets:
  GND: Part1.GND, S1.COM, S2.COM, NEOPIXEL1.GND
  N1: Part1.RAW, NEOPIXEL1.+5V
  N2: Part1.D11_PWM/MOSI, S1.L1
  N3: Part1.D8, S2.L1
  N4: Part1.D2, NEOPIXEL1.Din

custom parts:
  Neopixel Strip -- White (30/m): These NeoPixel strips have 30 digitally-addressable pixel LEDs per meter and are very affordable and are only 12.5 mm wide, 10 mm if you remove the strip from the casing.
